# Fritzing sketch ironman (saved by Fritzing 0.9.3b)
breadboards: 1

parts:
  Parça1 = Arduino Nano (Rev3.0)
  Parça2 = Humidity Sensor - HIH-4030 Breakout
  Parça3 = Humidity Sensor - HIH-4030 Breakout
  R1 = Resistor [tolerance=±5% resistance=220 package=THT]
  LED1 = smd LED [color="White (8000K)" package="0805 [SMD]"]  # not connected
  R2 = Resistor [tolerance=±5% resistance=220 package=THT]  # not connected
  LED2 = smd LED [color="White (8000K)" package="0805 [SMD]"]  # not connected
  R3 = Resistor [tolerance=±5% resistance=220 package=THT]
  LED3 = smd LED [color="White (8000K)" package="0805 [SMD]"]  # not connected
  R4 = Resistor [tolerance=±5% resistance=220 package=THT]  # not connected
  LED4 = smd LED [color="White (8000K)" package="0805 [SMD]"]  # not connected
  R5 = Resistor [tolerance=±5% resistance=220 package=THT]  # not connected
  LED5 = smd LED [color="White (8000K)" package="0805 [SMD]"]  # not connected
  R6 = Resistor [tolerance=±5% resistance=220 package=THT]
  LED6 = smd LED [color="White (8000K)" package="0805 [SMD]"]
  R7 = Resistor [tolerance=±5% resistance=220 package=THT]
  R8 = Resistor [tolerance=±5% resistance=220 package=THT]  # not connected
  R9 = Resistor [tolerance=±5% resistance=220 package=THT]  # not connected
  R10 = Resistor [tolerance=±5% resistance=220 package=THT]  # not connected
  R11 = Resistor [tolerance=±5% resistance=220 package=THT]
  R12 = Resistor [tolerance=±5% resistance=220 package=THT]
  LED7 = smd LED [color="White (8000K)" package="0805 [SMD]"]  # not connected
  LED8 = smd LED [color="White (8000K)" package="0805 [SMD]"]  # not connected
  LED9 = smd LED [color="White (8000K)" package="0805 [SMD]"]  # not connected
  LED10 = smd LED [color="White (8000K)" package="0805 [SMD]"]  # not connected
  LED11 = smd LED [color="White (8000K)" package="0805 [SMD]"]  # not connected
  LED12 = smd LED [color="White (8000K)" package="0805 [SMD]"]  # not connected
  J1 = Piezo Speaker
  J2 = Basic Servo
  VCC2 = Battery block 9V
  Parça4 = Bluetooth HC-05 Macho

nets:
  N1: Parça1.D1/TX, Parça4.RXD
  N2: Parça1.D0/RX, Parça4.TXD
  GND: Parça1.GND, Parça3.GND, LED6.cathode, J1.pin1, J2.gnd, VCC2.-, Parça4.GND
  N3: Parça1.D2, Parça3.VCC
  N4: Parça1.D3, Parça2.VCC
  N5: Parça1.D4, R6.Pin_1
  N6: Parça1.D5, R3.Pin_1
  N7: Parça1.D6, R1.Pin_1
  N8: Parça1.D7, R12.Pin_1
  N9: Parça1.D8, R11.Pin_1
  N10: Parça1.D9, R7.Pin_1
  N11: Parça1.D10, J2.pulse
  N12: Parça1.D11/MOSI, J1.pin2
  N13: Parça1.VIN, VCC2.+
  5V: Parça1.5V, J2.vcc
  3V3: Parça1.3V3, Parça4.VCC
